# Fritzing sketch ColetaDadosFritzing (saved by Fritzing 0.9.3b)
breadboards: 1

parts:
  R1 = Resistor [tolerance=±5% resistance=10k package=THT]
  Mod1 = Voltage Sensor 25V
  Componente3 = Arduino Uno (Rev3)
  ZS-042_RTC3 = ZS-042 RTC Module
  microSD2 = MicroSD Card Module
  Mod5 = Voltage Sensor 25V
  R2 = Resistor [tolerance=±5% resistance=10k package=THT]
  Part4 = Solar Panel [package="Renogy 50 Watts 12 Volt Monocrystalline Bendable Solar Panel"]
  Part5 = Solar Panel [package="Renogy 50 Watts 12 Volt Monocrystalline Bendable Solar Panel"]

nets:
  GND: R1.Pin_0, Mod1.GND, Mod1.-, Componente3.GND, ZS-042_RTC3.GND, Mod5.GND, Mod5.-, R2.Pin_1, Part4.Connector_2, Part5.Connector_2
  N1: R1.Pin_1, Mod1.VCC, Part4.Connector_1
  N2: Mod1.S, Componente3.A0
  N3: Componente3.A1, Mod5.S
  N4: Componente3.D11_PWM/MOSI, microSD2.MOSI
  N5: Componente3.D12/MISO, microSD2.MISO
  N6: Componente3.D13/SCK, microSD2.SCK
  N7: Componente3.A4/SDA, ZS-042_RTC3.SDA
  N8: Componente3.A5/SCL, ZS-042_RTC3.SCL
  N9: Componente3.D4, microSD2.CS
  5V: Componente3.5V, ZS-042_RTC3.VCC
  N10: Mod5.VCC, R2.Pin_0, Part5.Connector_1

custom parts:
  Solar Panel: Renogy 50 Watts 12 Volt Solar Panel
