# Fritzing sketch Untitled Sketch (saved by Fritzing 0.9.3b)
breadboards: 1

parts:
  Componente1 = Arduino Mega 2560 (Rev3)
  ZS-042_RTC1 = ZS-042 RTC Module
  SM1 = 28BYJ-48 Stepper Motor [part_number=28BYJ-48]
  Driver1 = 28BYJ-48 Driver Module [part_number=ULN2003 package=THT]
  Componente2 = Arduino Uno (Rev3)
  ZS-042_RTC2 = ZS-042 RTC Module
  microSD1 = MicroSD Card Module
  R1 = Resistor [tolerance=±10% resistance=10k package=THT]
  Mod2 = Voltage Sensor 25V
  Part3 = Solar Panel [package="Renogy 50 Watts 12 Volt Monocrystalline Bendable Solar Panel"]
  J1 = Basic Servo
  Part4 = Solar Panel [package="Renogy 50 Watts 12 Volt Monocrystalline Bendable Solar Panel"]
  Mod4 = Voltage Sensor 25V
  R3 = Resistor [tolerance=±10% resistance=10k package=THT]

nets:
  N1: Componente1.D21/SCL, ZS-042_RTC1.SCL
  N2: Componente1.D20/SDA, ZS-042_RTC1.SDA
  N3: Componente1.D11_PWM, J1.pulse
  N4: Componente1.D9_PWM, Driver1.IN4
  N5: Componente1.D8_PWM, Driver1.IN3
  VCC: Componente1.5V, ZS-042_RTC1.VCC, J1.vcc
  GND: Componente1.GND, ZS-042_RTC1.GND, J1.gnd
  N6: Componente1.D6_PWM, Driver1.IN1
  N7: Componente1.D7_PWM, Driver1.IN2
  N8: SM1.blue-pin, Driver1.blue-pin
  N9: SM1.pink-pin, Driver1.pink-pin
  N10: SM1.yellow-pin, Driver1.yellow-pin
  N11: SM1.orange-pin, Driver1.orange-pin
  N12: SM1.red-pin, Driver1.red-pin
  N13: Componente2.A0, Mod2.S
  N14: Componente2.A1, Mod4.S
  N15: Componente2.D11_PWM/MOSI, microSD1.MOSI
  N16: Componente2.D12/MISO, microSD1.MISO
  N17: Componente2.D13/SCK, microSD1.SCK
  N18: Componente2.A4/SDA, ZS-042_RTC2.SDA
  N19: Componente2.A5/SCL, ZS-042_RTC2.SCL
  N20: Componente2.D4, microSD1.CS
  VCC_2: Componente2.5V, ZS-042_RTC2.VCC, microSD1.VCC
  GND_2: Componente2.GND, ZS-042_RTC2.GND, microSD1.GND, R1.Pin_0, Mod2.GND, Mod2.-, Part3.Connector_2, Part4.Connector_1, Mod4.GND, Mod4.-, R3.Pin_1
  N21: R1.Pin_1, Mod2.VCC, Part3.Connector_1
  N22: Part4.Connector_2, Mod4.VCC, R3.Pin_0

custom parts:
  28BYJ-48 Stepper Motor: Unipolar Stepper Motor 28BYJ-48 Top coil - pink & orange Bottom coil - blue & yellow Common rail - red Connector pins: blue - pink - yellow - orange - red
  28BYJ-48 Driver Module: High-power ULN2003 Stepper Motor Driver Board Test Module For Arduino AVR SMD
  Solar Panel: Renogy 50 Watts 12 Volt Solar Panel
